# Fritzing sketch esp32_temp (saved by Fritzing 0.9.3b)

parts:
  M1 = DOIT Esp32 DevKit v1 (30 pins long, 11 pins width) [part_number=ESP32S-PIN30]
  SSD1306 = OLED 128x64 I2C Monochrome Display
  BME280 = Adafruit BME280
  Touch_Sensor = TOUCH [package=touch1]

nets:
  3V3: M1.3V3, SSD1306.VDD, BME280.3.3V
  GND: M1.GND, SSD1306.GND, BME280.GND
  N1: M1.D15, Touch_Sensor.T2
  N2: M1.D18, BME280.SDI/SDA
  N3: M1.D19, BME280.SCK/SCL
  N4: M1.D21, SSD1306.SDA
  N5: M1.D22, SSD1306.SCK

custom parts:
  DOIT Esp32 DevKit v1 (30 pins long, 11 pins width): The DOIT Esp32 DevKit v1 is one of the development board created by DOIT to evaluate the ESP-WROOM-32 module. It is based on the ESP32 microcontroller that boasts Wifi, Bluetooth, Ethernet and Low Power support all in a single chip. (vanepp) made breadboard work, adjusted pin numbering and labels and reduced size of schematic and cleaned up pcb. This chip is 30pins long (2 x15) and 11 pins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
  Adafruit BME280: Bosch has stepped up their game with their new BME280 sensor, an environmental sensor with temperature, barometric pressure and humidity! This sensor is great for all sorts of weather/environmental sensing and can even be used in both I2C and SPI! This precision sensor from Bosch is the best low-cost sensing solution for measuring humidity with ±3% accuracy, barometric pressure with ±1 hPa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
